# Fritzing sketch door_controller (saved by Fritzing 0.9.3b)
circuit board: 9.80568cm x 8.03737cm
breadboards: 1

parts:
  Not = NPN-Transistor [package="TO92 [THT]"]
  X1 = USB Connectors [package=usb-a-s]
  R2 = Resistor [tolerance=±5% resistance=220 package=THT]
  R1 = Resistor [tolerance=±0.05% resistance=4.7k package=THT]
  Boot = Toggle Switch [package=THT]
  Power = Toggle Switch [package=THT]
  IC1 = H-Bridge [package=THT]
  IC2 = SO14 [chip_label=IC package=SO]  # not connected
  U3 = TPS73633 [package=sot23-5]
  Motor_Enable = NPN-Transistor [package="TO92 [THT]"]
  Part2 = ESP-WROOM-32 [ESP-32S] Module [part_number=ESP-WROOM-32]
  Motor_Direction = NPN-Transistor [package="TO92 [THT]"]
  C2 = Tantalum Capacitor [capacitance=10nF package="100 mil [THT, tantalum]"]
  C3 = Electrolytic Capacitor [capacitance=10µF package="200 mil [THT, electrolytic]"]
  R3 = Resistor [tolerance=±0.05% resistance=4.7k package=THT]
  R4 = Resistor [tolerance=±0.05% resistance=4.7k package=THT]
  U1 = mystery part, 6 pins [chip_label="Lock Interface"]
  BAT1 = 18650 battery holder [package=battery-18650-kit]  # not connected

nets:
  GND: Not.E, X1.GND, Boot.COM, IC1.GND1, IC1.GND2, IC1.GND3, IC1.GND4, U3.GND, Part2.GND, C2.+, C3.-
  N1: Not.B, R1.Pin_1, IC1.4A
  N2: Not.C, R2.Pin_1, IC1.3A
  N3: X1.D+, Part2.RXD0
  N4: X1.D-, Part2.TXD0
  N5: X1.VBUS, Power.L2
  N6: R2.Pin_0, Power.COM, IC1.VCC2, IC1.VCC1, U3.IN, U3.EN, Motor_Enable.C, Part2.EN, Motor_Direction.C
  N7: R1.Pin_0, Motor_Direction.E
  N8: Boot.L1, Part2.IO0
  N9: IC1.3_4EN, Motor_Enable.E
  N10: IC1.3Y, U1.pin5
  N11: IC1.4Y, U1.pin4
  N12: U3.NR/FB, C2.-
  N13: U3.OUT, Part2.3V3, C3.+
  N14: Motor_Enable.B, R3.Pin_1
  N15: Part2.IO33, R4.Pin_1
  N16: Part2.IO25, R3.Pin_0
  N17: Part2.IO26, U1.pin6
  N18: Part2.IO27, U1.pin2
  N19: Part2.IO14, U1.pin1
  N20: Part2.IO12, U1.pin3
  N21: Motor_Direction.B, R4.Pin_0

custom parts:
  TPS73633: Cap-Free, NMOS, 400-mA Low-Dropout Regulator with Reverse Current Protection
  ESP-WROOM-32 [ESP-32S] Module: Espressif ESP-WROOM-32 WiFi/Bluetooth LE microcontroller module also known as the Ai-Thinker ESP-32S module with similar formfactor. The ESP32 is a microcontroller chip with WiFi and BLE capabilities. The chip is developed by Espressif and is the successor to the popular ESP8266 WiFi module.
  18650 battery holder: 18650 Battery Holder
